# Fritzing sketch TinyLoadr_Shield_v2.5h (saved by Fritzing 0.8.3b)
circuit board: 7.13529cm x 5.33527cm

parts:
  Arduino2 = Arduino [part_number=ATTiny]
  R1 = Resistor [tolerance=±5% resistance=10k package=THT]
  R5 = Resistor [tolerance=±5% resistance=680 package=THT]
  R4 = Resistor [tolerance=±5% resistance=680 package=THT]
  R3 = Resistor [tolerance=±5% resistance=10k package=THT]
  R2 = Resistor [tolerance=±5% resistance=10k package=THT]
  16MHz = Crystal [frequency="16 Mhz" package=THT]
  C1 = Ceramic Capacitor [capacitance=22pF voltage=10V package="100 mil [THT, multilayer]"]
  C2 = Ceramic Capacitor [capacitance=22pF voltage=10V package="100 mil [THT, multilayer]"]
  25/45/85/*314 = IC, DIP package, 12 pins [spacing=300mil part_number=ATtiny chip_label=25/45/85/*314]
  168/328 = IC, DIP package, 12 pins [chip_label=328 spacing=300mil part_number=ATmega]
  24/44/85 = IC, DIP package, 12 pins [chip_label=24/44/84 spacing=300mil part_number=ATtiny]
  Jumper3 = male pin header, 3 pins [form="♂ (male)"]
  Jumper2 = male pin header, 3 pins [form="♂ (male)"]
  Jumper1 = male pin header, 3 pins [form="♂ (male)"]
  Blink = LED - 3mm [color="Blue (525nm)" part_number=LED package="3 mm [THT]"]
  C3 = Electrolytic Capacitor [capacitance=10µF voltage=25V package="100 mil [THT, electrolytic]"]
  Reset = Pushbutton [package="[THT]"]
  Prog = LED - 3mm [color="Blue (525nm)" package="3 mm [THT]"]
  Error = LED - 3mm [color="Red (660nm)" package="3 mm [THT]"]
  Heart = LED - 3mm [color="Yellow (595nm)" part_number=beat package="3 mm [THT]"]
  Auto = male pin header, 3 pins [form="♂ (male)" part_number=Reset]
  28-Pin_ZIF_Socket = 28-Pin ZIF Socket from SparkFun [part_number=PRT-09175]

nets:
  N1: Arduino2.GND, R1.Pin_1, R5.Pin_0, R4.Pin_0, R3.Pin_0, C1.1, C2.0, 25/45/85/*314.pin2, 168/328.pin5, 24/44/85.pin2, C3.-, Reset.Pin_3, Reset.Pin_4
  N2: Arduino2.D13, 25/45/85/*314.pin5, 168/328.pin3, 24/44/85.pin5
  N3: Arduino2.D12, 25/45/85/*314.pin4, 24/44/85.pin4, 28-Pin_ZIF_Socket.Pin_18
  N4: Arduino2.D11, 25/45/85/*314.pin3, 24/44/85.pin3, 28-Pin_ZIF_Socket.Pin_17
  N5: Arduino2.D10, R2.Pin_1, 25/45/85/*314.pin6, 168/328.pin6, 24/44/85.pin6, Reset.Pin_1, Reset.Pin_2
  N6: Arduino2.D9, Heart.anode
  N7: Arduino2.D8, Error.anode
  N8: Arduino2.D7, Prog.anode
  N9: Arduino2.RST, Auto.pin2
  N10: Arduino2.+5V, R2.Pin_0, 25/45/85/*314.pin1, 168/328.pin4, 24/44/85.pin1
  N11: R1.Pin_0, Blink.cathode
  N12: R5.Pin_1, Heart.cathode
  N13: R4.Pin_1, Error.cathode
  N14: R3.Pin_1, Prog.cathode
  N15: 16MHz.pin_0, C2.1, 168/328.pin1
  N16: 16MHz.pin_1, C1.0, 168/328.pin2
  N17: 25/45/85/*314.pin7, 168/328.pin7, 24/44/85.pin12, 28-Pin_ZIF_Socket.Pin_1
  N18: 25/45/85/*314.pin8, 28-Pin_ZIF_Socket.Pin_27
  N19: 25/45/85/*314.pin9, 28-Pin_ZIF_Socket.Pin_26
  N20: 25/45/85/*314.pin10, 28-Pin_ZIF_Socket.Pin_25
  N21: 25/45/85/*314.pin11, 24/44/85.pin7, Jumper1.pin2
  N22: 25/45/85/*314.pin12, 24/44/85.pin11, 28-Pin_ZIF_Socket.Pin_28
  N23: 168/328.pin8, 24/44/85.pin9, Jumper3.pin2, 28-Pin_ZIF_Socket.Pin_22
  N24: 168/328.pin9, 24/44/85.pin10, Jumper2.pin2, 28-Pin_ZIF_Socket.Pin_20
  N25: 168/328.pin10, 28-Pin_ZIF_Socket.Pin_19
  N26: 168/328.pin11, Jumper1.pin3, 28-Pin_ZIF_Socket.Pin_10
  N27: 168/328.pin12, 28-Pin_ZIF_Socket.Pin_9
  N28: 24/44/85.pin8, 28-Pin_ZIF_Socket.Pin_23
  N29: Jumper3.pin1, 28-Pin_ZIF_Socket.Pin_8
  N30: Jumper2.pin1, 28-Pin_ZIF_Socket.Pin_7
  N31: Jumper1.pin1, 28-Pin_ZIF_Socket.Pin_4
  N32: Blink.anode, 28-Pin_ZIF_Socket.Pin_3
  N33: C3.+, Auto.pin3

notes:
  Shield v2.5
  TinyLoadr
  ATmega168/328
  ATtiny24/44/84
  ATtiny25/45/85/*313
  *313
  --
  Other
  ATtiny
  ON
  ---
  OFF
  ------------------------------------------
  | ** Turn on ONLY ONE group at a time! ** |
  Design by
  Jeff Murchison
  Special thanks to Mickey Poppitz for helping out with the schematic view.

custom parts:
  28-Pin ZIF Socket from SparkFun: A 28-pin slim ZIF socket, ordered from Sparkfun.
